// Logisim project brachocpu.circ as structural Verilog
module cpu (
  input  Reset,
  input  DataDebugEnable,
  input  AddressDebugEnable,
  input  ControlDebugEnable,
  input  [11:0] AddressBus,
  input  [15:0] DataBus,
  input  AO,
  input  BO,
  input  CO,
  input  ACO,
  input  IOD,
  input  PO,
  input  LO,
  input  IOA,
  input  AI,
  input  BI,
  input  CI,
  input  II,
  input  PI,
  input  LI,
  input  PID,
  input  INC,
  input  DisabledReset,
  input  CinALU,
  input  RI,
  input  RO,
  output out_27,
  output out_28,
  output out_29,
  output out_30,
  output out_31,
  output out_32,
  output out_33,
  output out_34,
  output out_35,
  output out_36,
  output out_37,
  output out_38,
  output out_39,
  output out_40,
  output out_41,
  output out_42,
  output out_43,
  output out_44,
  output out_45,
  output out_46
);

  wire controlunit_1_cout, MAINCLOCK_out;
  wire [2:0] alu_1_zero;
  wire [7:0] registerbank_1_irout;
  wire [11:0] controlled_buffer_1_out;
  wire [15:0] alu_1_acc, controlled_buffer_3_out, ram_1_dout, registerbank_1_balu, registerbank_1_calu;
  wire [16:0] controlled_buffer_2_out;
  wire [19:17] controlled_buffer_2_out_2;

  assign controlled_buffer_1_out = AddressDebugEnable ? AddressBus : 12'bz;  // Controlled_Buffer controlled_buffer_1
  assign {controlled_buffer_2_out_2, controlled_buffer_2_out} = ControlDebugEnable ? {RO, RI, CinALU, DisabledReset, INC, PID, LI, PI, II, CI, BI, AI, IOA, LO, PO, IOD, ACO, CO, BO, AO} : 20'bz;  // Controlled_Buffer controlled_buffer_2
  assign controlled_buffer_3_out = DataDebugEnable ? DataBus : 16'bz;  // Controlled_Buffer controlled_buffer_3
  Pull_Resistor pull_resistor_1 (.node({controlled_buffer_2_out_2, controlled_buffer_2_out}));
  Pull_Resistor pull_resistor_2 (.node(controlled_buffer_3_out));
  Clock MAINCLOCK (.out(MAINCLOCK_out));
  Pull_Resistor pull_resistor_3 (.node(controlled_buffer_1_out));
  // Probe on {controlled_buffer_2_out_2, controlled_buffer_2_out}
  // Probe on controlled_buffer_3_out
  // Probe on controlled_buffer_1_out
  ALU alu_1 (
    .Cin(controlled_buffer_2_out_2[17]), .B(registerbank_1_balu), .C(registerbank_1_calu),
    .op(registerbank_1_irout[3:0]), .ACC(alu_1_acc), .ZERO(alu_1_zero[0]), .NEGATIVE(alu_1_zero[1]),
    .OVERFLOW(alu_1_zero[2]));
  // Probe on alu_1_acc
  // Probe on registerbank_1_irout[3:0]
  RegisterBank registerbank_1 (
    .COUT(controlunit_1_cout), .Clear(Reset), .CLK(MAINCLOCK_out), .ACC(alu_1_acc),
    .AddressBusIN(controlled_buffer_1_out), .ControlBus(controlled_buffer_2_out),
    .DataBusIN(controlled_buffer_3_out), .AddressBusOUT(controlled_buffer_1_out),
    .DataBusOUT(controlled_buffer_3_out), .IRout(registerbank_1_irout), .BALU(registerbank_1_balu),
    .CALU(registerbank_1_calu));  // open: DataOUT, AO, BO, CO, ACO, IOD, PO, LO, IOA, AI, BI, CI, II, PI, LI, PID, INC, RESET, CinALU, RI, RO
  ControlUnit controlunit_1 (
    .Flag(alu_1_zero), .IRout(registerbank_1_irout), .Clear(Reset), .CLK(MAINCLOCK_out),
    .COUT(controlunit_1_cout),
    .ControlBus({out_46, out_45, out_44, out_43, out_42, out_41, out_40, out_39, out_38, out_37, out_36, out_35, out_34, out_33, out_32, out_31, out_30, out_29, out_28, out_27}));  // open: HALT
  // Probe on ram_1_dout
  assign {controlled_buffer_2_out_2, controlled_buffer_2_out} = {out_46, out_45, out_44, out_43, out_42, out_41, out_40, out_39, out_38, out_37, out_36, out_35, out_34, out_33, out_32, out_31, out_30, out_29, out_28, out_27};  // Buffer buffer_1, 20 bits wide
  Pull_Resistor pull_resistor_4 (.node({out_46, out_45, out_44, out_43, out_42, out_41, out_40, out_39, out_38, out_37, out_36, out_35, out_34, out_33, out_32, out_31, out_30, out_29, out_28, out_27}));
  assign controlled_buffer_3_out = controlled_buffer_2_out_2[19] ? ram_1_dout : 16'bz;  // Controlled_Buffer controlled_buffer_4
  RAM #(.addrWidth(12), .dataWidth(16), .trigger("high"), .\type ("nonvolatile")) ram_1 (
    .addr(controlled_buffer_1_out), .we(controlled_buffer_2_out_2[18]), .oe(1'b1),
    .din(controlled_buffer_3_out), .dout(ram_1_dout));
endmodule

module ALU (
  input  Cin,
  input  [15:0] B,
  input  [15:0] C,
  input  [3:0] op,
  output [15:0] ACC,
  output ZERO,
  output NEGATIVE,
  output OVERFLOW
);

  wire adder_1_cout, comparator_1_eq, not_2_out, sixteeninputor_1_out_2, sixteeninputor_2_out_2;
  wire [15:0] adder_1_out, and_1_out, divider_1_out, multiplier_1_cout, multiplier_1_out, not_1_out,
       or_1_out, shifter_1_out, shifter_2_out, subtractor_1_out, xor_1_out;

  assign not_1_out = ~B;  // NOT_Gate not_1, 16 bits wide
  assign and_1_out = B & C;  // AND_Gate and_1, 16 bits wide
  assign or_1_out = B | C;  // OR_Gate or_1, 16 bits wide
  Adder #(.width(16)) adder_1 (.a(B), .b(C), .out(adder_1_out), .cin(Cin), .cout(adder_1_cout));
  Subtractor #(.width(16)) subtractor_1 (.a(B), .b(C), .out(subtractor_1_out));  // open: bin, bout
  Multiplier #(.width(16)) multiplier_1 (
    .a(B), .b(C), .out(multiplier_1_out), .cin({16{1'b0}}), .cout(multiplier_1_cout));
  Divider #(.width(16)) divider_1 (.a(B), .b(C), .out(divider_1_out), .upper({16{1'b0}}));  // open: rem
  assign xor_1_out = B ^ C;  // XOR_Gate xor_1, 16 bits wide
  Shifter #(.width(16)) shifter_1 (.in(B), .\dist (C[3:0]), .out(shifter_1_out));
  Shifter #(.shift("lr"), .width(16)) shifter_2 (.in(B), .\dist (C[3:0]), .out(shifter_2_out));
  Comparator #(.width(16)) comparator_1 (.a(B), .b(C), .eq(comparator_1_eq), .lt(NEGATIVE));  // open: gt
  Multiplexer #(.select(4), .width(16)) multiplexer_1 (
    .in0(adder_1_out), .in1(subtractor_1_out), .in2(multiplier_1_out), .in3(divider_1_out), .in4(not_1_out),
    .in5(and_1_out), .in6(or_1_out), .in7(shifter_1_out), .in8(shifter_2_out), .in9(xor_1_out),
    .in10({16{1'b0}}), .in11({16{1'b0}}), .in12({16{1'b0}}), .in13({16{1'b0}}), .in14({16{1'b0}}),
    .in15({16{1'b0}}), .out(ACC), .sel(op));
  SixteenInputOR sixteeninputor_1 (.in_1(multiplier_1_cout), .out_2(sixteeninputor_1_out_2));
  SixteenInputOR sixteeninputor_2 (.in_1(ACC), .out_2(sixteeninputor_2_out_2));
  not not_2 (not_2_out, sixteeninputor_2_out_2);
  or or_2 (ZERO, not_2_out, comparator_1_eq);
  or or_3 (OVERFLOW, adder_1_cout, sixteeninputor_1_out_2);
endmodule

module RegisterBank (
  input  [11:0] AddressBusIN,
  input  [15:0] DataBusIN,
  input  [16:0] ControlBus,
  input  COUT,
  input  [15:0] ACC,
  input  CLK,
  input  Clear,
  output [11:0] AddressBusOUT,
  output [15:0] DataBusOUT,
  output AO,
  output [15:0] DataOUT,
  output BO,
  output CO,
  output ACO,
  output IOD,
  output PO,
  output LO,
  output IOA,
  output [15:0] BALU,
  output AI,
  output BI,
  output CI,
  output II,
  output PI,
  output LI,
  output PID,
  output [15:0] CALU,
  output INC,
  output RESET,
  output CinALU,
  output RI,
  output RO,
  output [7:0] IRout
);

  wire [6:0] pull_resistor_1_node;
  wire [7:0] InstructionRegister_q;
  wire [11:0] LinkRegister_q, programcounter_1_addressbusout;
  wire [15:0] accumulator_q, bit_extender_1_out, RegisterA_q;

  // Probe on ControlBus[14]
  // Probe on ControlBus[15]
  // Probe on pull_resistor_1_node
  // Probe on ControlBus[13:8]
  Pull_Resistor pull_resistor_1 (.node(pull_resistor_1_node));
  assign pull_resistor_1_node = Clear ? {7{1'b1}} : 7'bz;  // Controlled_Buffer controlled_buffer_1
  // Probe on ControlBus[16]
  Register #(.width(12)) LinkRegister (
    .D(AddressBusIN), .en(ControlBus[13]), .clk(CLK), .Q(LinkRegister_q), .clr(pull_resistor_1_node[6]));
  Register #(.width(16)) RegisterA (
    .D(DataBusIN), .en(ControlBus[8]), .clk(CLK), .Q(RegisterA_q), .clr(pull_resistor_1_node[0]));
  Register #(.width(16)) RegisterB (
    .D(DataBusIN), .en(ControlBus[9]), .clk(CLK), .Q(BALU), .clr(pull_resistor_1_node[1]));
  Register #(.width(16)) RegisterC (
    .D(DataBusIN), .en(ControlBus[10]), .clk(CLK), .Q(CALU), .clr(pull_resistor_1_node[2]));
  Register #(.width(16)) accumulator (.D(ACC), .en(1'b1), .clk(CLK), .Q(accumulator_q), .clr(pull_resistor_1_node[3]));
  Register #(.width(16)) InstructionRegister (
    .D(DataBusIN), .en(ControlBus[11]), .clk(CLK), .Q({IRout, InstructionRegister_q}),
    .clr(pull_resistor_1_node[4]));
  Pull_Resistor pull_resistor_2 (.node(ControlBus));
  assign DataBusOUT = ControlBus[1] ? BALU : 16'bz;  // Controlled_Buffer controlled_buffer_2
  assign DataBusOUT = ControlBus[2] ? CALU : 16'bz;  // Controlled_Buffer controlled_buffer_3
  assign DataBusOUT = ControlBus[3] ? accumulator_q : 16'bz;  // Controlled_Buffer controlled_buffer_4
  assign DataBusOUT = ControlBus[4] ? bit_extender_1_out : 16'bz;  // Controlled_Buffer controlled_buffer_5
  assign bit_extender_1_out = {{4{1'b0}}, {IRout[3:0], InstructionRegister_q}};  // Bit_Extender bit_extender_1
  // Probe on ControlBus[7:0]
  assign DataBusOUT = ControlBus[0] ? RegisterA_q : 16'bz;  // Controlled_Buffer controlled_buffer_6
  Programcounter programcounter_1 (
    .DataBus(DataBusIN), .AdressBus(AddressBusIN), .PIDATA(ControlBus[14]), .INC(ControlBus[15]),
    .PI(ControlBus[12]), .CLK(CLK), .R(pull_resistor_1_node[5]),
    .AddressBusOUT(programcounter_1_addressbusout));
  assign AddressBusOUT = ControlBus[6] ? LinkRegister_q : 12'bz;  // Controlled_Buffer controlled_buffer_7
  assign AddressBusOUT = ControlBus[7] ? {IRout[3:0], InstructionRegister_q} : 12'bz;  // Controlled_Buffer controlled_buffer_8
  assign AddressBusOUT = ControlBus[5] ? programcounter_1_addressbusout : 12'bz;  // Controlled_Buffer controlled_buffer_9
  // Probe on programcounter_1_addressbusout
  assign DataOUT = COUT ? RegisterA_q : 16'bz;  // Controlled_Buffer controlled_buffer_10

  assign ACO = ControlBus[3];
  assign AI = ControlBus[8];
  assign AO = ControlBus[0];
  assign BI = ControlBus[9];
  assign BO = ControlBus[1];
  assign CI = ControlBus[10];
  assign CO = ControlBus[2];
  assign II = ControlBus[11];
  assign INC = ControlBus[15];
  assign IOA = ControlBus[7];
  assign IOD = ControlBus[4];
  assign LI = ControlBus[13];
  assign LO = ControlBus[6];
  assign PI = ControlBus[12];
  assign PID = ControlBus[14];
  assign PO = ControlBus[5];
  assign RESET = ControlBus[16];

  // Notes on the sheet:
  //   DataOUT: pull=down
endmodule

module Programcounter (
  input  [15:0] DataBus,
  input  [11:0] AdressBus,
  input  PIDATA,
  input  INC,
  input  PI,
  input  CLK,
  input  R,
  output [11:0] AddressBusOUT
);

  wire counter_1_carry, not_1_out, or_1_out;
  wire [15:0] controlled_buffer_1_out;

  or or_1 (or_1_out, counter_1_carry, R);
  assign controlled_buffer_1_out = PIDATA ? DataBus : 16'bz;  // Controlled_Buffer controlled_buffer_1
  assign controlled_buffer_1_out[11:0] = not_1_out ? AdressBus : 12'bz;  // Controlled_Buffer controlled_buffer_2
  not not_1 (not_1_out, PIDATA);
  Counter #(.max('hfff), .width(12)) counter_1 (
    .clr(or_1_out), .load(PI), .up(1'b1), .count(INC), .clk(CLK), .D(controlled_buffer_1_out[11:0]),
    .carry(counter_1_carry), .Q(AddressBusOUT));
endmodule

module SixteenInputOR (
  input  [15:0] in_1,
  output out_2
);

  or or_1 (out_2, in_1[0], in_1[1], in_1[2], in_1[3], in_1[4], in_1[5], in_1[6], in_1[7], in_1[8], in_1[9], in_1[10], in_1[11], in_1[12], in_1[13], in_1[14], in_1[15]);
endmodule

module ControlUnit (
  input  [2:0] Flag,
  input  [7:0] IRout,
  input  Clear,
  input  CLK,
  output COUT,
  output HALT,
  output [19:0] ControlBus
);

  wire and_2_out, bnflag_1_br, not_1_out, not_2_out, not_3_out;
  wire [1:0] counter_1_q;
  wire [4:0] bnflag_1_brout, multiplexer_1_out, multiplexer_2_out;

  not not_1 (not_1_out, CLK);
  and and_1 (Clear, counter_1_q[0], counter_1_q[1]);
  Counter #(.max('h3), .width(2)) counter_1 (
    .clr(Clear), .load(1'b0), .up(1'b1), .count(1'b1), .clk(not_1_out), .D(2'b00), .Q(counter_1_q));  // open: carry
  BnFlag bnflag_1 (.code(IRout[7:4]), .Flags(Flag), .BR(bnflag_1_br), .BROUT(bnflag_1_brout));
  Multiplexer #(.width(5)) multiplexer_1 (
    .in0({4'b0000, counter_1_q[0]}), .in1({1'b1, IRout[7:4]}), .out(multiplexer_1_out), .sel(counter_1_q[1]));
  Multiplexer #(.width(5)) multiplexer_2 (
    .in0(bnflag_1_brout), .in1(multiplexer_1_out), .out(multiplexer_2_out), .sel(not_2_out));
  not not_2 (not_2_out, bnflag_1_br);
  ROM #(.addrWidth(5), .dataWidth(20)) rom_1 (.addr(multiplexer_2_out), .data(ControlBus));
  and and_2 (and_2_out, IRout[4], IRout[6], IRout[7]);
  not not_3 (not_3_out, IRout[5]);
  and and_3 (COUT, not_3_out, and_2_out);
  and and_4 (HALT, IRout[5], and_2_out);

  // Notes on the sheet:
  //   ControlBus: pull=up
  //   Clear: pull=down
  //   contents of rom_1 (hex, n*v repeats v):
  //   80820 8000 15*0 210 410 80280 80480 40081 1080 0 0 0 1040 0 0 0 108
endmodule

module ControlBusSchema (
  input  AO,
  input  BO,
  input  CO,
  input  ACO,
  input  IOD,
  input  PO,
  input  LO,
  input  IOA,
  input  AI,
  input  BI,
  input  CI,
  input  II,
  input  PI,
  input  LI,
  input  PID,
  input  INC,
  input  RESET,
  input  CinALU,
  input  RI,
  input  RO
);

  // Probe on {RO, RI, CinALU, RESET, INC, PID, LI, PI, II, CI, BI, AI, IOA, LO, PO, IOD, ACO, CO, BO, AO}
endmodule

module BnFlag (
  input  [3:0] code,
  input  [2:0] Flags,
  output BR,
  output [4:0] BROUT
);

  wire and_1_out, and_2_out, and_3_out, and_4_out, and_5_out, and_6_out, not_1_out, not_2_out, not_3_out,
       not_4_out, not_5_out, not_6_out, or_2_out;

  // Probe on Flags[2]
  // Probe on Flags[1]
  // Probe on Flags[0]
  not not_1 (not_1_out, code[3]);
  not not_2 (not_2_out, code[2]);
  not not_3 (not_3_out, code[0]);
  not not_4 (not_4_out, code[1]);
  not not_5 (not_5_out, code[2]);
  not not_6 (not_6_out, code[1]);
  and and_1 (and_1_out, not_3_out, not_4_out, not_5_out, code[3]);
  and and_2 (and_2_out, code[0], code[1], code[2], not_1_out);
  and and_3 (and_3_out, code[0], code[3], not_6_out, not_2_out);
  // Probe on and_1_out
  // Probe on and_2_out
  // Probe on and_3_out
  and and_4 (and_4_out, and_1_out, Flags[0]);
  and and_5 (and_5_out, and_2_out, Flags[1]);
  and and_6 (and_6_out, and_3_out, Flags[2]);
  or or_1 (BR, and_1_out, and_2_out, and_3_out);
  or or_2 (or_2_out, and_4_out, and_5_out, and_6_out);
  Multiplexer #(.width(5)) multiplexer_1 (.in0(5'b11110), .in1(5'b10110), .out(BROUT), .sel(or_2_out));

  // Notes on the sheet:
  //   NOP instruction
endmodule
